// Logisim project 2^n%5.circ as structural Verilog: 4 circuits, main circuit mod5
module mod5 (
  input  In,
  output S0,
  output S1,
  output S2,
  output S3,
  output S4
);

  wire clock_1_out, next_logistics_1_t0, next_logistics_1_t1, register_1_q, register_2_q;
  wire [2:0] decoder_1_e;

  next_logistics next_logistics_1 (
    .S1(register_1_q), .S0(register_2_q), .Input(In), .T1(next_logistics_1_t1), .T0(next_logistics_1_t0));
  Register #(.width(1)) register_1 (.D(next_logistics_1_t1), .Q(register_1_q), .clk(clock_1_out));  // open: en, clr
  Register #(.width(1)) register_2 (.D(next_logistics_1_t0), .Q(register_2_q), .clk(clock_1_out));  // open: en, clr
  decoder decoder_1 (
    .a(next_logistics_1_t1), .b(next_logistics_1_t0), .c(decoder_1_e[2]), .d(decoder_1_e[1]),
    .e(decoder_1_e[0]));
  Clock clock_1 (.out(clock_1_out));
  // Probe on decoder_1_e
  Decoder #(.select(3), .enable("false")) decoder_2 (
    .out1(S1), .out2(S2), .out3(S3), .out4(S4), .sel(decoder_1_e));  // open: out0, out5, out6, out7

  assign S0 = 1'b0;
endmodule

module next_logistics (
  input  S1,
  input  S0,
  input  Input,
  output T1,
  output T0
);

  wire and_1_out, and_2_out, and_3_out, and_4_out, and_5_out, and_6_out, not_1_out, not_2_out, not_3_out,
       not_4_out, not_5_out, not_6_out, not_7_out, not_8_out;

  not not_1 (not_1_out, S1);
  not not_2 (not_2_out, S0);
  not not_3 (not_3_out, S1);
  not not_4 (not_4_out, S0);
  not not_5 (not_5_out, S1);
  not not_6 (not_6_out, Input);
  not not_7 (not_7_out, S0);
  not not_8 (not_8_out, Input);
  and and_1 (and_1_out, not_1_out, S0);
  and and_2 (and_2_out, S1, not_2_out);
  and and_3 (and_3_out, not_3_out, not_4_out, Input);
  and and_4 (and_4_out, not_5_out, S0, not_6_out);
  and and_5 (and_5_out, S1, not_7_out, not_8_out);
  and and_6 (and_6_out, S1, S0, Input);
  or or_1 (T1, and_1_out, and_2_out);
  or or_2 (T0, and_3_out, and_4_out, and_5_out, and_6_out);
endmodule

module decoder (
  input  a,
  input  b,
  output c,
  output d,
  output e
);

  wire and_2_out, and_3_out, not_1_out, not_2_out;

  and and_1 (c, a, b);
  not not_1 (not_1_out, a);
  not not_2 (not_2_out, b);
  not not_3 (e, b);
  and and_2 (and_2_out, not_1_out, b);
  and and_3 (and_3_out, a, not_2_out);
  or or_1 (d, and_2_out, and_3_out);
endmodule

module test (
  input  [3:0] in_1,
  output out_2,
  output out_3,
  output out_4,
  output out_5,
  output out_6,
  output out_7
);

  wire clock_1_out;
  wire [3:0] register_1_q;

  Register #(.width(4)) register_1 (.D(in_1), .Q(register_1_q), .clk(clock_1_out));  // open: en, clr
  Clock clock_1 (.out(clock_1_out));
  ROM #(.addrWidth(4), .dataWidth(1)) rom_1 (.addr(register_1_q), .data(out_2));  // open: sel
  mod5 mod5_1 (.In(out_2), .S0(out_3), .S1(out_4), .S2(out_5), .S3(out_6), .S4(out_7));
endmodule
