// Logisim project jjj.circ as structural Verilog: 3 circuits, main circuit main
module main (
  input  in0,
  input  in1,
  input  pre0,
  input  pre1,
  output out0,
  output out1
);

  wire and_1_out, and_2_out, and_3_out, and_4_out, and_5_out, and_6_out, not_1_out, not_2_out, not_3_out,
       not_4_out;

  not not_1 (not_1_out, in1);
  not not_2 (not_2_out, pre0);
  not not_3 (not_3_out, in0);
  not not_4 (not_4_out, pre1);
  and and_1 (and_1_out, not_1_out, not_2_out, pre1);
  and and_2 (and_2_out, in0, not_4_out, not_1_out);
  and and_3 (and_3_out, pre0, not_3_out, not_4_out);
  and and_4 (and_4_out, not_3_out, not_2_out, pre1, in1);
  and and_5 (and_5_out, pre1, pre0, not_1_out, in0);
  and and_6 (and_6_out, pre1, not_2_out, not_3_out);
  or or_1 (out0, and_1_out, and_2_out, and_4_out, and_5_out);
  or or_2 (out1, and_6_out, and_3_out);
endmodule

module fsm (
  input  [1:0] in_1,
  input  clr,
  input  clk,
  output out_4,
  output [1:0] out_5,
  output [1:0] out_6
);

  wire and_1_out, output_1_out_5, register_1_q;

  main main_1 (.in0(in_1[0]), .in1(in_1[1]), .pre0(out_5[0]), .pre1(out_5[1]), .out0(out_6[0]), .out1(out_6[1]));
  Register #(.width(1)) register_1 (.D(clr), .Q(register_1_q), .clk(clk));  // open: en, clr
  Register #(.width(2)) register_2 (.D(out_6), .Q(out_5), .clk(clk), .clr(and_1_out));  // open: en
  and and_1 (and_1_out, register_1_q, clr);
  \output  output_1 (.in_1(in_1[0]), .in_2(in_1[1]), .in_3(out_5[0]), .in_4(out_5[1]), .out_5(output_1_out_5));
  Multiplexer multiplexer_1 (.in0(output_1_out_5), .in1(1'b0), .out(out_4), .sel(and_1_out));  // open: en
endmodule

module \output  (
  input  in_1,
  input  in_2,
  input  in_3,
  input  in_4,
  output out_5
);

  wire and_1_out, and_2_out, and_3_out, not_1_out, not_2_out, not_3_out, not_4_out, or_1_out, or_2_out;

  or or_1 (or_1_out, in_2, in_1);
  not not_1 (not_1_out, in_1);
  and and_1 (and_1_out, in_3, in_4);
  not not_2 (not_2_out, in_3);
  not not_3 (not_3_out, or_1_out);
  not not_4 (not_4_out, and_1_out);
  and and_2 (and_2_out, not_1_out, in_2);
  or or_2 (or_2_out, not_3_out, and_2_out);
  and and_3 (and_3_out, not_2_out, in_4);
  and and_4 (out_5, or_2_out, not_4_out, and_3_out);
endmodule
