// Logisim project register.circ as structural Verilog: 2 circuits, main circuit grf
module grf (
  input  in_1,
  input  in_2,
  input  in_3,
  input  [4:0] in_4,
  input  [4:0] in_5,
  input  [4:0] in_6,
  input  [31:0] in_7,
  output [31:0] out_8,
  output [31:0] out_9
);

  wire en0, en1, en2, en3;
  wire [2:0] demultiplexer_1_out0, demultiplexer_1_out1, demultiplexer_1_out2, demultiplexer_1_out3,
       demultiplexer_2_out0, demultiplexer_2_out1, demultiplexer_2_out2, demultiplexer_2_out3,
       demultiplexer_3_out0, demultiplexer_3_out1, demultiplexer_3_out2, demultiplexer_3_out3;
  wire [31:0] n8re_1_out_10, n8re_1_out_11, n8re_2_out_10, n8re_2_out_11, n8re_3_out_10, n8re_3_out_11,
       n8re_4_out_10, n8re_4_out_11;

  Demultiplexer #(.select(2), .width(3), .tristate("true")) demultiplexer_1 (
    .out0(demultiplexer_1_out0), .out1(demultiplexer_1_out1), .out2(demultiplexer_1_out2),
    .out3(demultiplexer_1_out3), .in(in_5[2:0]), .sel(in_5[4:3]));  // open: en
  Demultiplexer #(.select(2), .width(3), .tristate("true")) demultiplexer_2 (
    .out0(demultiplexer_2_out0), .out1(demultiplexer_2_out1), .out2(demultiplexer_2_out2),
    .out3(demultiplexer_2_out3), .in(in_4[2:0]), .sel(in_4[4:3]));  // open: en
  Demultiplexer #(.select(2), .width(3), .tristate("true")) demultiplexer_3 (
    .out0(demultiplexer_3_out0), .out1(demultiplexer_3_out1), .out2(demultiplexer_3_out2),
    .out3(demultiplexer_3_out3), .in(in_6[2:0]), .sel(in_6[4:3]));  // open: en
  Decoder #(.select(2), .tristate("true")) decoder_1 (
    .out0(en0), .out1(en1), .out2(en2), .out3(en3), .sel(in_6[4:3]), .en(in_1));
  _8re u_8re_1 (
    .WD(in_7), .En1(in_1), .Reaet(in_3), .ck(in_2), .in_2(1'b0), .en(en0), .A3(demultiplexer_3_out0),
    .A1(demultiplexer_2_out0), .A2(demultiplexer_1_out0), .out_10(n8re_1_out_10), .out_11(n8re_1_out_11));
  _8re u_8re_2 (
    .WD(in_7), .En1(in_1), .Reaet(in_3), .ck(in_2), .in_2(1'b1), .en(en1), .A3(demultiplexer_3_out1),
    .A1(demultiplexer_2_out1), .A2(demultiplexer_1_out1), .out_10(n8re_2_out_10), .out_11(n8re_2_out_11));
  _8re u_8re_3 (
    .WD(in_7), .En1(in_1), .Reaet(in_3), .ck(in_2), .in_2(1'b1), .en(en2), .A3(demultiplexer_3_out2),
    .A1(demultiplexer_2_out2), .A2(demultiplexer_1_out2), .out_10(n8re_3_out_10), .out_11(n8re_3_out_11));
  _8re u_8re_4 (
    .WD(in_7), .En1(in_1), .Reaet(in_3), .ck(in_2), .in_2(1'b1), .en(en3), .A3(demultiplexer_3_out3),
    .A1(demultiplexer_2_out3), .A2(demultiplexer_1_out3), .out_10(n8re_4_out_10), .out_11(n8re_4_out_11));
  Multiplexer #(.select(2), .width(32)) multiplexer_1 (
    .in0(n8re_1_out_10), .in1(n8re_2_out_10), .in2(n8re_3_out_10), .in3(n8re_4_out_10), .out(out_8),
    .sel(in_4[4:3]));  // open: en
  Multiplexer #(.select(2), .width(32)) multiplexer_2 (
    .in0(n8re_1_out_11), .in1(n8re_2_out_11), .in2(n8re_3_out_11), .in3(n8re_4_out_11), .out(out_9),
    .sel(in_5[4:3]));  // open: en

  // Other names for the same wires on the sheet: clk = in_2; En = in_1; slt1[1:0] = in_4[4:3]; slt2[1:0] = in_5[4:3];
  //   Reset = in_3; wd[31:0] = in_7
endmodule

module _8re (
  input  ck,
  input  in_2,
  input  [31:0] WD,
  input  En1,
  input  Reaet,
  input  en,
  input  [2:0] A3,
  input  [2:0] A1,
  input  [2:0] A2,
  output [31:0] out_10,
  output [31:0] out_11
);

  wire and_1_out, and_2_out, not_1_out;
  wire [1:0] demultiplexer_1_out0, demultiplexer_1_out1, demultiplexer_2_out0, demultiplexer_2_out1,
       demultiplexer_3_out0, demultiplexer_3_out1;
  wire [31:0] _0, _1, _2, _3, _4, _5, _6, _7, demultiplexer_4_out0, demultiplexer_4_out1,
       demultiplexer_4_out2, demultiplexer_4_out3, demultiplexer_5_out0, demultiplexer_5_out1,
       demultiplexer_5_out2, demultiplexer_5_out3, multiplexer_1_out, multiplexer_2_out, multiplexer_3_out,
       multiplexer_4_out;

  and and_1 (and_1_out, in_2, and_2_out);
  and and_2 (and_2_out, En1, en);
  Register #(.width(32)) register_1 (.D(demultiplexer_4_out0), .en(and_1_out), .Q(_0), .clk(ck), .clr(Reaet));
  Register #(.width(32)) register_2 (.D(demultiplexer_5_out0), .en(and_2_out), .Q(_4), .clk(ck), .clr(Reaet));
  Register #(.width(32)) register_3 (.D(demultiplexer_4_out1), .en(and_2_out), .Q(_1), .clk(ck), .clr(Reaet));
  Register #(.width(32)) register_4 (.D(demultiplexer_5_out1), .en(and_2_out), .Q(_5), .clk(ck), .clr(Reaet));
  Demultiplexer #(.width(2), .tristate("true")) demultiplexer_1 (
    .out0(demultiplexer_1_out0), .out1(demultiplexer_1_out1), .in(A3[1:0]), .sel(A3[2]));  // open: en
  Demultiplexer #(.width(2), .tristate("true")) demultiplexer_2 (
    .out0(demultiplexer_2_out0), .out1(demultiplexer_2_out1), .in(A1[1:0]), .sel(A1[2]));  // open: en
  Demultiplexer #(.width(2), .tristate("true")) demultiplexer_3 (
    .out0(demultiplexer_3_out0), .out1(demultiplexer_3_out1), .in(A2[1:0]), .sel(A2[2]));  // open: en
  Register #(.width(32)) register_5 (.D(demultiplexer_4_out2), .en(and_2_out), .Q(_2), .clk(ck), .clr(Reaet));
  Register #(.width(32)) register_6 (.D(demultiplexer_5_out2), .en(and_2_out), .Q(_6), .clk(ck), .clr(Reaet));
  Register #(.width(32)) register_7 (.D(demultiplexer_4_out3), .en(and_2_out), .Q(_3), .clk(ck), .clr(Reaet));
  Register #(.width(32)) register_8 (.D(demultiplexer_5_out3), .en(and_2_out), .Q(_7), .clk(ck), .clr(Reaet));
  Demultiplexer #(.select(2), .width(32), .tristate("true")) demultiplexer_4 (
    .out0(demultiplexer_4_out0), .out1(demultiplexer_4_out1), .out2(demultiplexer_4_out2),
    .out3(demultiplexer_4_out3), .in(WD), .sel(demultiplexer_1_out0), .en(not_1_out));
  not not_1 (not_1_out, A3[2]);
  Demultiplexer #(.select(2), .width(32), .tristate("true")) demultiplexer_5 (
    .out0(demultiplexer_5_out0), .out1(demultiplexer_5_out1), .out2(demultiplexer_5_out2),
    .out3(demultiplexer_5_out3), .in(WD), .sel(demultiplexer_1_out1), .en(A3[2]));
  Multiplexer #(.select(2), .width(32)) multiplexer_1 (
    .in0(_4), .in1(_5), .in2(_6), .in3(_7), .out(multiplexer_1_out), .sel(demultiplexer_2_out1));  // open: en
  Multiplexer #(.select(2), .width(32)) multiplexer_2 (
    .in0(_0), .in1(_1), .in2(_2), .in3(_3), .out(multiplexer_2_out), .sel(demultiplexer_3_out0));  // open: en
  Multiplexer #(.select(2), .width(32)) multiplexer_3 (
    .in0(_0), .in1(_1), .in2(_2), .in3(_3), .out(multiplexer_3_out), .sel(demultiplexer_2_out0));  // open: en
  Multiplexer #(.select(2), .width(32)) multiplexer_4 (
    .in0(_4), .in1(_5), .in2(_6), .in3(_7), .out(multiplexer_4_out), .sel(demultiplexer_3_out1));  // open: en
  Multiplexer #(.width(32)) multiplexer_5 (
    .in0(multiplexer_3_out), .in1(multiplexer_1_out), .out(out_10), .sel(A1[2]));  // open: en
  Multiplexer #(.width(32)) multiplexer_6 (
    .in0(multiplexer_2_out), .in1(multiplexer_4_out), .out(out_11), .sel(A2[2]));  // open: en

  // Other names for the same wires on the sheet: wd1[31:0] = WD
endmodule
