// Logisim project seller.circ as structural Verilog: 2 circuits, main circuit main
module main (
  input  [2:0] in_1,
  input  in_2,
  output out_3,
  output out_4,
  output out_5
);

  wire clock_1_out, comparator_1_lt, comparator_2_gt, multiplexer_1_out, not_1_out, or_1_out;
  wire [3:0] add_1_out_3, register_1_q, register_2_q, subtractor_1_out;
  wire [3:3] multiplexer_2_out;

  // Probe on add_1_out_3
  add add_1 (.in_1(in_1), .pre(register_1_q), .out_3(add_1_out_3));
  // Probe on register_1_q
  Register #(.width(4)) register_1 (.D(add_1_out_3), .Q(register_1_q), .clk(clock_1_out), .clr(or_1_out));  // open: en
  or or_1 (or_1_out, multiplexer_1_out, in_2);
  Multiplexer multiplexer_1 (.in0(1'b0), .in1(not_1_out), .out(multiplexer_1_out), .sel(not_1_out));  // open: en
  Clock clock_1 (.out(clock_1_out));
  Comparator #(.width(4), .mode("unsigned")) comparator_1 (
    .a(register_1_q), .b(4'b0101), .lt(comparator_1_lt));  // open: gt, eq
  Subtractor #(.width(4)) subtractor_1 (.a(register_1_q), .b(4'b0101), .out(subtractor_1_out));  // open: bin, bout
  not not_1 (not_1_out, comparator_2_gt);
  Comparator #(.width(4), .mode("unsigned")) comparator_2 (
    .a(4'b0101), .b(register_2_q), .gt(comparator_2_gt));  // open: eq, lt
  Register #(.width(4)) register_2 (.D(register_1_q), .Q(register_2_q), .clk(clock_1_out));  // open: en, clr
  Multiplexer #(.width(4)) multiplexer_2 (
    .in0(subtractor_1_out), .in1(4'b0000), .out({multiplexer_2_out[3], out_5, out_4, out_3}),
    .sel(comparator_1_lt));  // open: en
endmodule

module add (
  input  [2:0] in_1,
  input  [3:0] pre,
  output [3:0] out_3
);

  wire [3:0] bit_extender_1_out;

  assign bit_extender_1_out = {{1{1'b0}}, in_1};  // Bit_Extender bit_extender_1
  Adder #(.width(4)) adder_1 (.a(bit_extender_1_out), .b(pre), .out(out_3));  // open: cin, cout
endmodule
