// Logisim project single_cycle_cpu.circ as structural Verilog: 8 circuits, main circuit IFU
module IFU (
  input  PCsrc,
  input  Reset,
  input  Clk,
  input  Jsrc,
  input  Jadr,
  input  [31:0] JADDR,
  output [31:0] Instr,
  output [31:0] PC_4
);

  wire [1:0] demultiplexer_1_out0;
  wire [31:0] adder_2_out, bit_extender_1_out, multiplexer_1_out, multiplexer_2_out, register_1_q,
       shifter_1_out, undriven;

  // Probe on multiplexer_2_out
  Multiplexer #(.width(32)) multiplexer_1 (
    .in0(multiplexer_2_out), .in1(adder_2_out), .out(multiplexer_1_out), .sel(PCsrc));  // open: en
  Register #(.width(32)) register_1 (.D(multiplexer_1_out), .Q(register_1_q), .clk(Clk), .clr(Reset));  // open: en
  Multiplexer #(.width(32)) multiplexer_2 (
    .in0(PC_4), .in1(undriven), .out(multiplexer_2_out), .sel(Jsrc));  // open: en
  Demultiplexer #(.width(32)) demultiplexer_1 (
    .out0({register_1_q[31:28], Instr[25:0], demultiplexer_1_out0}), .out1(JADDR), .in(undriven), .sel(Jadr));  // open: en
  Adder #(.width(32)) adder_1 (.a(register_1_q), .b(32'h4), .out(PC_4));  // open: cin, cout
  ROM #(.addrWidth(5), .dataWidth(32)) rom_1 (.addr(register_1_q[6:2]), .data(Instr));  // open: sel
  assign bit_extender_1_out = {{16{Instr[15]}}, Instr[15:0]};  // Bit_Extender bit_extender_1
  Shifter #(.width(32)) shifter_1 (.in(bit_extender_1_out), .\dist (5'b00010), .out(shifter_1_out));
  Adder #(.width(32)) adder_2 (.a(shifter_1_out), .b(PC_4), .out(adder_2_out));  // open: cin, cout
  // also tied to GND on the sheet: {demultiplexer_1_out0[0], demultiplexer_1_out0[1]}

  // Notes on the sheet:
  //   contents of rom_1 (hex, n*v repeats v):
  //   341c0000 341d0000 340080f8 36ee0367 3593769c 34dda539 3465c5dc 34be0ff1 3472af1d 35566602 35fe72a7
  //   3437ff23 37b9649e 3690bf9b 37fe4e0c 3711f49d 3c113bfe 3c057433 3c03c451 3c04c431 3c1c24d9 3c1bf0da
  //   3c0ccc68 3c0a118d 3c1021ea 3c0004d3 3c16115b 3c184f06 3c1215de 1000ffff
endmodule

module ALU (
  input  [3:0] ALUop,
  input  [31:0] SrcA,
  input  [31:0] SrcB,
  input  [4:0] Shift,
  output B_bigger,
  output B_equal,
  output B_smaller,
  output [31:0] ALUResult
);

  wire [0:0] comparator_1_lt, comparator_2_lt;
  wire [31:0] adder_1_out, and_1_out, nor_1_out, or_1_out, shifter_1_out, shifter_2_out, shifter_3_out,
       shifter_4_out, shifter_5_out, shifter_6_out, subtractor_1_out, xor_1_out;

  Adder #(.width(32)) adder_1 (.a(SrcA), .b(SrcB), .out(adder_1_out));  // open: cin, cout
  Subtractor #(.width(32)) subtractor_1 (.a(SrcA), .b(SrcB), .out(subtractor_1_out));  // open: bin, bout
  assign or_1_out = SrcA | SrcB;  // OR_Gate or_1, 32 bits wide
  assign and_1_out = SrcA & SrcB;  // AND_Gate and_1, 32 bits wide
  assign nor_1_out = ~(SrcA | SrcB);  // NOR_Gate nor_1, 32 bits wide
  assign xor_1_out = SrcA ^ SrcB;  // XOR_Gate xor_1, 32 bits wide
  Comparator #(.width(32)) comparator_1 (.a(SrcA), .b(SrcB), .lt(comparator_1_lt[0]));  // open: gt, eq
  Comparator #(.width(32), .mode("unsigned")) comparator_2 (
    .a(SrcA), .b(SrcB), .lt(comparator_2_lt[0]));  // open: gt, eq
  Shifter #(.width(32)) shifter_1 (.in(SrcB), .\dist (Shift), .out(shifter_1_out));
  Shifter #(.width(32)) shifter_2 (.in(SrcB), .\dist (SrcA[4:0]), .out(shifter_2_out));
  Shifter #(.width(32), .shift("ar")) shifter_3 (.in(SrcB), .\dist (Shift), .out(shifter_3_out));
  Shifter #(.width(32), .shift("ar")) shifter_4 (.in(SrcB), .\dist (SrcA[4:0]), .out(shifter_4_out));
  Shifter #(.width(32), .shift("lr")) shifter_5 (.in(SrcB), .\dist (Shift), .out(shifter_5_out));
  Shifter #(.width(32), .shift("lr")) shifter_6 (.in(SrcB), .\dist (SrcA[4:0]), .out(shifter_6_out));
  Multiplexer #(.select(4), .width(32), .enable("false")) multiplexer_1 (
    .in0(adder_1_out), .in1(subtractor_1_out), .in2(or_1_out), .in3(and_1_out), .in4(nor_1_out),
    .in5(xor_1_out), .in6({{31{1'b0}}, comparator_1_lt[0]}), .in7({{31{1'b0}}, comparator_2_lt[0]}),
    .in8(shifter_1_out), .in9(shifter_2_out), .in10(shifter_3_out), .in11(shifter_4_out),
    .in12(shifter_5_out), .in13(shifter_6_out), .out(ALUResult), .sel(ALUop));  // open: in14, in15
  Comparator #(.width(32)) comparator_3 (.a(ALUResult), .b({32{1'b0}}), .gt(B_bigger), .eq(B_equal), .lt(B_smaller));
endmodule

// 2
module DM (
  input  [2:0] L_Stype,
  input  [31:0] Addr,
  input  Wen,
  input  Clk,
  input  Reset,
  input  [31:0] WD,
  output [31:0] RD
);

  wire [7:0] multiplexer_5_out;
  wire [15:0] multiplexer_4_out, ram_1_data;
  wire [31:0] bit_extender_1_out, bit_extender_2_out, multiplexer_1_out, multiplexer_2_out,
       multiplexer_3_out, shifter_1_out;
  wire [31:16] ram_1_data_2;

  Shifter #(.width(32), .shift("ar")) shifter_1 (.in(Addr), .\dist (5'b00010), .out(shifter_1_out));
  Multiplexer #(.width(32)) multiplexer_1 (
    .in0({ram_1_data_2, WD[15:0]}), .in1({WD[31:16], ram_1_data}), .out(multiplexer_1_out), .sel(Addr[1]));  // open: en
  Multiplexer #(.select(3), .width(32)) multiplexer_2 (
    .in0(WD), .in1(multiplexer_1_out), .in2(multiplexer_3_out), .out(multiplexer_2_out), .sel(L_Stype));  // open: in3, in4, in5, in6, in7, en
  Multiplexer #(.select(2), .width(32), .enable("false")) multiplexer_3 (
    .in0({ram_1_data_2, ram_1_data[15:8], WD[7:0]}), .in1({ram_1_data_2, WD[7:0], ram_1_data[7:0]}),
    .in2({ram_1_data_2[31:24], WD[7:0], ram_1_data}), .in3({WD[7:0], ram_1_data_2[23:16], ram_1_data}),
    .out(multiplexer_3_out), .sel(Addr[1:0]));
  RAM #(.addrWidth(5), .dataWidth(32), .bus("separate")) ram_1 (
    .addr(shifter_1_out[4:0]), .din(multiplexer_2_out), .data({ram_1_data_2, ram_1_data}), .str(Wen),
    .clk(Clk), .ld(1'b1), .clr(Reset));  // open: sel
  Multiplexer #(.width(16)) multiplexer_4 (
    .in0(ram_1_data), .in1(ram_1_data_2), .out(multiplexer_4_out), .sel(Addr[1]));  // open: en
  Multiplexer #(.select(2), .width(8), .enable("false")) multiplexer_5 (
    .in0(ram_1_data[7:0]), .in1(ram_1_data[15:8]), .in2(ram_1_data_2[23:16]), .in3(ram_1_data_2[31:24]),
    .out(multiplexer_5_out), .sel(Addr[1:0]));
  assign bit_extender_1_out = {{16{multiplexer_4_out[15]}}, multiplexer_4_out};  // Bit_Extender bit_extender_1
  assign bit_extender_2_out = {{24{multiplexer_5_out[7]}}, multiplexer_5_out};  // Bit_Extender bit_extender_2
  Multiplexer #(.select(3), .width(32)) multiplexer_6 (
    .in0({ram_1_data_2, ram_1_data}), .in1(bit_extender_1_out), .in2({{16{1'b0}}, multiplexer_4_out}),
    .in3(bit_extender_2_out), .in4({{24{1'b0}}, multiplexer_5_out}), .out(RD), .sel(L_Stype));  // open: in5, in6, in7, en
endmodule

module EXT (
  input  [1:0] EXTop,
  input  [15:0] In,
  output [31:0] Out
);

  wire [31:0] bit_extender_1_out, bit_extender_2_out;

  assign bit_extender_1_out = {{16{1'b0}}, In};  // Bit_Extender bit_extender_1
  assign bit_extender_2_out = {{16{In[15]}}, In};  // Bit_Extender bit_extender_2
  Multiplexer #(.select(2), .width(32)) multiplexer_1 (
    .in0(bit_extender_1_out), .in1(bit_extender_2_out), .in2({In, {16{1'b0}}}), .out(Out), .sel(EXTop));  // open: in3, en
endmodule

module Controller (
  input  Op5,
  input  Op4,
  input  Op3,
  input  Op2,
  input  Op1,
  input  Op0,
  input  Funct5,
  input  Funct4,
  input  Funct3,
  input  Funct2,
  input  Funct1,
  input  Funct0,
  output RegWriteEN,
  output RegDst,
  output ALUop0,
  output ALUop1,
  output ALUSrc,
  output PCsrc,
  output MemtoReg,
  output MemWrite,
  output branch0,
  output Ext0,
  output Ext1,
  output pc_4toreg,
  output Jaddr,
  output Jsrc,
  output bgez
);

  wire addu_out, beq_out, bgez_out, jalr_out, jr_out, lui_out, lw_out, not_1_out, not_2_out, not_3_out,
       not_4_out, not_5_out, not_6_out, not_7_out, not_8_out, not_9_out, not_10_out, not_11_out, not_12_out,
       ori_out, subu_out, sw_out;

  not not_1 (not_1_out, Op5);
  not not_2 (not_2_out, Op3);
  not not_3 (not_3_out, Op4);
  not not_4 (not_4_out, Op1);
  not not_5 (not_5_out, Op2);
  not not_6 (not_6_out, Op0);
  not not_7 (not_7_out, Funct5);
  not not_8 (not_8_out, Funct4);
  not not_9 (not_9_out, Funct3);
  not not_10 (not_10_out, Funct2);
  not not_11 (not_11_out, Funct1);
  not not_12 (not_12_out, Funct0);
  and addu (addu_out, not_6_out, not_4_out, not_5_out, not_2_out, not_3_out, not_1_out, Funct0, not_11_out, not_10_out, not_9_out, not_8_out, Funct5);
  and subu (subu_out, not_6_out, not_4_out, not_5_out, not_2_out, not_3_out, not_1_out, Funct0, Funct1, not_10_out, not_9_out, not_8_out, Funct5);
  and ori (ori_out, Op0, not_4_out, Op2, Op3, not_3_out, not_1_out);
  and lw (lw_out, Op0, Op1, not_5_out, not_2_out, not_3_out, Op5);
  and sw (sw_out, Op0, Op1, not_5_out, Op3, not_3_out, Op5);
  and beq (beq_out, not_6_out, not_4_out, Op2, not_2_out, not_3_out, not_1_out);
  and lui (lui_out, Op0, Op1, Op2, Op3, not_3_out, not_1_out);
  and jalr (jalr_out, not_6_out, not_4_out, not_5_out, not_2_out, not_3_out, not_1_out, Funct0, not_11_out, not_10_out, Funct3, not_8_out, not_7_out);
  and jr (jr_out, not_6_out, not_4_out, not_5_out, not_2_out, not_3_out, not_1_out, not_12_out, not_11_out, not_10_out, Funct3, not_8_out, not_7_out);
  and u_bgez (bgez_out, Op0, not_4_out, not_5_out, not_2_out, not_3_out, not_1_out);
  // AND_Gate nop has open pins: in0=not_6_out, in1=not_4_out, in2=not_5_out, in3=not_2_out, in4=not_3_out, in5=not_1_out, out=open
  or or_1 (RegWriteEN, jalr_out, addu_out, subu_out, ori_out, lw_out, lui_out);
  or or_2 (RegDst, jalr_out, subu_out, addu_out);
  or or_3 (ALUop0, subu_out, beq_out);
  or or_4 (ALUop1, ori_out, lui_out);
  or or_5 (ALUSrc, ori_out, lw_out, sw_out, lui_out, jalr_out);
  buf or_6 (MemtoReg, lw_out);  // OR_Gate
  buf or_7 (PCsrc, beq_out);  // OR_Gate
  buf or_8 (MemWrite, sw_out);  // OR_Gate
  buf or_9 (branch0, beq_out);  // OR_Gate
  or or_10 (Ext0, lw_out, sw_out, beq_out);
  buf or_11 (Ext1, lui_out);  // OR_Gate
  buf or_12 (pc_4toreg, jalr_out);  // OR_Gate
  or or_13 (Jaddr, jalr_out, jr_out);
  or or_14 (Jsrc, jalr_out, jr_out);
  buf or_15 (bgez, bgez_out);  // OR_Gate
endmodule

module main (
  input  Reset,
  output [31:0] out_2,
  output out_3,
  output [4:0] out_4,
  output [31:0] out_5,
  output out_6,
  output [4:0] out_7,
  output [31:0] out_8
);

  wire alu_1_b_bigger, alu_1_b_equal, alu_1_b_smaller, Clk, controller_1_alusrc, controller_1_bgez,
       controller_1_branch0, controller_1_jaddr, controller_1_jsrc, controller_1_memtoreg,
       controller_1_pc_4toreg, controller_1_regdst, multiplexer_5_out, or_1_out, or_2_out, or_3_out;
  wire [1:0] controller_1_aluop0, controller_1_ext0;
  wire [2:0] bit_extender_1_out;
  wire [3:0] bit_extender_2_out;
  wire [31:0] alu_1_aluresult, dm_1_rd, ext_1_out, grf_1_rd1, ifu_1_pc_4, multiplexer_3_out,
       multiplexer_4_out, multiplexer_6_out, shifter_1_out;

  Clock clock_1 (.out(Clk));
  IFU ifu_1 (
    .Reset(Reset), .JADDR(grf_1_rd1), .Instr(out_2), .PCsrc(multiplexer_5_out), .Jsrc(controller_1_jsrc),
    .Jadr(controller_1_jaddr), .Clk(Clk), .PC_4(ifu_1_pc_4));
  // Probe on out_2[25:21]
  Multiplexer #(.width(5)) multiplexer_1 (
    .in0(out_2[20:16]), .in1(out_2[15:11]), .out(out_4), .sel(controller_1_regdst));  // open: en
  Controller controller_1 (
    .Op5(out_2[31]), .Op4(out_2[30]), .Op3(out_2[29]), .Op2(out_2[28]), .Op1(out_2[27]), .Op0(out_2[26]),
    .Funct5(out_2[5]), .Funct4(out_2[4]), .Funct3(out_2[3]), .Funct2(out_2[2]), .Funct1(out_2[1]),
    .Funct0(out_2[0]), .RegWriteEN(out_3), .RegDst(controller_1_regdst), .ALUop0(controller_1_aluop0[0]),
    .ALUop1(controller_1_aluop0[1]), .ALUSrc(controller_1_alusrc), .MemtoReg(controller_1_memtoreg),
    .MemWrite(out_6), .branch0(controller_1_branch0), .Ext0(controller_1_ext0[0]),
    .Ext1(controller_1_ext0[1]), .pc_4toreg(controller_1_pc_4toreg), .Jaddr(controller_1_jaddr),
    .Jsrc(controller_1_jsrc), .bgez(controller_1_bgez));  // open: PCsrc
  Multiplexer #(.width(32)) multiplexer_2 (
    .in0(multiplexer_6_out), .in1(ifu_1_pc_4), .out(out_5), .sel(controller_1_pc_4toreg));  // open: en
  GRF grf_1 (
    .En(out_3), .R1(out_2[25:21]), .R2(out_2[20:16]), .Waddr(out_4), .WD(out_5), .RD1(grf_1_rd1),
    .RD2(out_8), .Reset(Reset), .Clk(Clk));
  assign bit_extender_1_out = {{2{1'b0}}, controller_1_branch0};  // Bit_Extender bit_extender_1
  assign bit_extender_2_out = {{2{1'b0}}, controller_1_aluop0};  // Bit_Extender bit_extender_2
  Multiplexer #(.width(32)) multiplexer_3 (
    .in0(out_8), .in1(ext_1_out), .out(multiplexer_3_out), .sel(controller_1_alusrc));  // open: en
  EXT ext_1 (.In(out_2[15:0]), .Out(ext_1_out), .EXTop(controller_1_ext0));
  // Probe on grf_1_rd1
  Multiplexer #(.width(32)) multiplexer_4 (
    .in0(multiplexer_3_out), .in1({32{1'b0}}), .out(multiplexer_4_out), .sel(controller_1_bgez));  // open: en
  // Probe on ext_1_out
  // Probe on bit_extender_2_out
  ALU alu_1 (
    .SrcA(grf_1_rd1), .SrcB(multiplexer_4_out), .Shift(out_2[10:6]), .B_bigger(alu_1_b_bigger),
    .B_equal(alu_1_b_equal), .B_smaller(alu_1_b_smaller), .ALUResult(alu_1_aluresult),
    .ALUop(bit_extender_2_out));
  or or_1 (or_1_out, alu_1_b_bigger, alu_1_b_equal);
  or or_2 (or_2_out, alu_1_b_equal, alu_1_b_smaller);
  or or_3 (or_3_out, alu_1_b_bigger, alu_1_b_smaller);
  Shifter #(.width(32), .shift("ar")) shifter_1 (.in(alu_1_aluresult), .\dist (5'b00010), .out(shifter_1_out));
  Bit_Extender #(.in_width(32), .out_width(5)) bit_extender_3 (.in(shifter_1_out), .out(out_7));
  DM dm_1 (.Addr(alu_1_aluresult), .WD(out_8), .RD(dm_1_rd), .Wen(out_6), .L_Stype(3'b000), .Clk(Clk), .Reset(Reset));
  Multiplexer #(.select(3)) multiplexer_5 (
    .in0(1'b0), .in1(alu_1_b_equal), .in2(or_1_out), .in3(alu_1_b_bigger), .in4(or_2_out),
    .in5(alu_1_b_smaller), .in6(or_3_out), .out(multiplexer_5_out), .sel(bit_extender_1_out));  // open: in7, en
  // Probe on alu_1_aluresult
  Multiplexer #(.width(32)) multiplexer_6 (
    .in0(alu_1_aluresult), .in1(dm_1_rd), .out(multiplexer_6_out), .sel(controller_1_memtoreg));  // open: en

  // Other names for the same wires on the sheet: Instr[31:0] = out_2; MemAddr[4:0] = out_7; MemData[31:0] = out_8;
  //   MemWrite = out_6; RegAddr[4:0] = out_4; RegData[31:0] = out_5; RegWrite = out_3
endmodule

module GRF (
  input  En,
  input  Clk,
  input  Reset,
  input  [4:0] R1,
  input  [4:0] R2,
  input  [4:0] Waddr,
  input  [31:0] WD,
  output [31:0] RD1,
  output [31:0] RD2
);

  wire en0, en1, en2, en3;
  wire [2:0] demultiplexer_1_out0, demultiplexer_1_out1, demultiplexer_1_out2, demultiplexer_1_out3,
       demultiplexer_2_out0, demultiplexer_2_out1, demultiplexer_2_out2, demultiplexer_2_out3,
       demultiplexer_3_out0, demultiplexer_3_out1, demultiplexer_3_out2, demultiplexer_3_out3;
  wire [31:0] n8re_1_out_10, n8re_1_out_11, n8re_2_out_10, n8re_2_out_11, n8re_3_out_10, n8re_3_out_11,
       n8re_4_out_10, n8re_4_out_11;

  Demultiplexer #(.select(2), .width(3)) demultiplexer_1 (
    .out0(demultiplexer_1_out0), .out1(demultiplexer_1_out1), .out2(demultiplexer_1_out2),
    .out3(demultiplexer_1_out3), .in(R2[2:0]), .sel(R2[4:3]));  // open: en
  Demultiplexer #(.select(2), .width(3)) demultiplexer_2 (
    .out0(demultiplexer_2_out0), .out1(demultiplexer_2_out1), .out2(demultiplexer_2_out2),
    .out3(demultiplexer_2_out3), .in(R1[2:0]), .sel(R1[4:3]));  // open: en
  Demultiplexer #(.select(2), .width(3)) demultiplexer_3 (
    .out0(demultiplexer_3_out0), .out1(demultiplexer_3_out1), .out2(demultiplexer_3_out2),
    .out3(demultiplexer_3_out3), .in(Waddr[2:0]), .sel(Waddr[4:3]));  // open: en
  Decoder #(.select(2)) decoder_1 (.out0(en0), .out1(en1), .out2(en2), .out3(en3), .sel(Waddr[4:3]), .en(En));
  _8re u_8re_1 (
    .WD(WD), .En1(En), .Reaet(Reset), .ck(Clk), .in_2(1'b0), .en(en0), .A3(demultiplexer_3_out0),
    .A1(demultiplexer_2_out0), .A2(demultiplexer_1_out0), .out_10(n8re_1_out_10), .out_11(n8re_1_out_11));
  _8re u_8re_2 (
    .WD(WD), .En1(En), .Reaet(Reset), .ck(Clk), .in_2(1'b1), .en(en1), .A3(demultiplexer_3_out1),
    .A1(demultiplexer_2_out1), .A2(demultiplexer_1_out1), .out_10(n8re_2_out_10), .out_11(n8re_2_out_11));
  _8re u_8re_3 (
    .WD(WD), .En1(En), .Reaet(Reset), .ck(Clk), .in_2(1'b1), .en(en2), .A3(demultiplexer_3_out2),
    .A1(demultiplexer_2_out2), .A2(demultiplexer_1_out2), .out_10(n8re_3_out_10), .out_11(n8re_3_out_11));
  _8re u_8re_4 (
    .WD(WD), .En1(En), .Reaet(Reset), .ck(Clk), .in_2(1'b1), .en(en3), .A3(demultiplexer_3_out3),
    .A1(demultiplexer_2_out3), .A2(demultiplexer_1_out3), .out_10(n8re_4_out_10), .out_11(n8re_4_out_11));
  Multiplexer #(.select(2), .width(32)) multiplexer_1 (
    .in0(n8re_1_out_10), .in1(n8re_2_out_10), .in2(n8re_3_out_10), .in3(n8re_4_out_10), .out(RD1),
    .sel(R1[4:3]));  // open: en
  Multiplexer #(.select(2), .width(32)) multiplexer_2 (
    .in0(n8re_1_out_11), .in1(n8re_2_out_11), .in2(n8re_3_out_11), .in3(n8re_4_out_11), .out(RD2),
    .sel(R2[4:3]));  // open: en

  // Other names for the same wires on the sheet: slt1[1:0] = R1[4:3]; slt2[1:0] = R2[4:3]
endmodule

module _8re (
  input  ck,
  input  in_2,
  input  [31:0] WD,
  input  En1,
  input  Reaet,
  input  en,
  input  [2:0] A3,
  input  [2:0] A1,
  input  [2:0] A2,
  output [31:0] out_10,
  output [31:0] out_11
);

  wire and_1_out, and_2_out, not_1_out;
  wire [1:0] demultiplexer_1_out0, demultiplexer_1_out1, demultiplexer_2_out0, demultiplexer_2_out1,
       demultiplexer_3_out0, demultiplexer_3_out1;
  wire [31:0] _0, _1, _2, _3, _4, _5, _6, _7, demultiplexer_4_out0, demultiplexer_4_out1,
       demultiplexer_4_out2, demultiplexer_4_out3, demultiplexer_5_out0, demultiplexer_5_out1,
       demultiplexer_5_out2, demultiplexer_5_out3, multiplexer_1_out, multiplexer_2_out, multiplexer_3_out,
       multiplexer_4_out;

  and and_1 (and_1_out, in_2, and_2_out);
  and and_2 (and_2_out, En1, en);
  Register #(.width(32)) register_1 (.D(demultiplexer_4_out0), .en(and_1_out), .Q(_0), .clk(ck), .clr(Reaet));
  Register #(.width(32)) register_2 (.D(demultiplexer_5_out0), .en(and_2_out), .Q(_4), .clk(ck), .clr(Reaet));
  Register #(.width(32)) register_3 (.D(demultiplexer_4_out1), .en(and_2_out), .Q(_1), .clk(ck), .clr(Reaet));
  Register #(.width(32)) register_4 (.D(demultiplexer_5_out1), .en(and_2_out), .Q(_5), .clk(ck), .clr(Reaet));
  Demultiplexer #(.width(2), .tristate("true")) demultiplexer_1 (
    .out0(demultiplexer_1_out0), .out1(demultiplexer_1_out1), .in(A3[1:0]), .sel(A3[2]));  // open: en
  Demultiplexer #(.width(2), .tristate("true")) demultiplexer_2 (
    .out0(demultiplexer_2_out0), .out1(demultiplexer_2_out1), .in(A1[1:0]), .sel(A1[2]));  // open: en
  Demultiplexer #(.width(2), .tristate("true")) demultiplexer_3 (
    .out0(demultiplexer_3_out0), .out1(demultiplexer_3_out1), .in(A2[1:0]), .sel(A2[2]));  // open: en
  Register #(.width(32)) register_5 (.D(demultiplexer_4_out2), .en(and_2_out), .Q(_2), .clk(ck), .clr(Reaet));
  Register #(.width(32)) register_6 (.D(demultiplexer_5_out2), .en(and_2_out), .Q(_6), .clk(ck), .clr(Reaet));
  Register #(.width(32)) register_7 (.D(demultiplexer_4_out3), .en(and_2_out), .Q(_3), .clk(ck), .clr(Reaet));
  Register #(.width(32)) register_8 (.D(demultiplexer_5_out3), .en(and_2_out), .Q(_7), .clk(ck), .clr(Reaet));
  Demultiplexer #(.select(2), .width(32), .tristate("true")) demultiplexer_4 (
    .out0(demultiplexer_4_out0), .out1(demultiplexer_4_out1), .out2(demultiplexer_4_out2),
    .out3(demultiplexer_4_out3), .in(WD), .sel(demultiplexer_1_out0), .en(not_1_out));
  not not_1 (not_1_out, A3[2]);
  Demultiplexer #(.select(2), .width(32), .tristate("true")) demultiplexer_5 (
    .out0(demultiplexer_5_out0), .out1(demultiplexer_5_out1), .out2(demultiplexer_5_out2),
    .out3(demultiplexer_5_out3), .in(WD), .sel(demultiplexer_1_out1), .en(A3[2]));
  Multiplexer #(.select(2), .width(32)) multiplexer_1 (
    .in0(_4), .in1(_5), .in2(_6), .in3(_7), .out(multiplexer_1_out), .sel(demultiplexer_2_out1));  // open: en
  Multiplexer #(.select(2), .width(32)) multiplexer_2 (
    .in0(_0), .in1(_1), .in2(_2), .in3(_3), .out(multiplexer_2_out), .sel(demultiplexer_3_out0));  // open: en
  Multiplexer #(.select(2), .width(32)) multiplexer_3 (
    .in0(_0), .in1(_1), .in2(_2), .in3(_3), .out(multiplexer_3_out), .sel(demultiplexer_2_out0));  // open: en
  Multiplexer #(.select(2), .width(32)) multiplexer_4 (
    .in0(_4), .in1(_5), .in2(_6), .in3(_7), .out(multiplexer_4_out), .sel(demultiplexer_3_out1));  // open: en
  Multiplexer #(.width(32)) multiplexer_5 (
    .in0(multiplexer_3_out), .in1(multiplexer_1_out), .out(out_10), .sel(A1[2]));  // open: en
  Multiplexer #(.width(32)) multiplexer_6 (
    .in0(multiplexer_2_out), .in1(multiplexer_4_out), .out(out_11), .sel(A2[2]));  // open: en

  // Other names for the same wires on the sheet: wd1[31:0] = WD
endmodule
