// Logisim project sort.circ as structural Verilog: 4 circuits, main circuit 1bit_swap
module _1bit_swap (
  input  l1,
  input  l2,
  input  S,
  output O1,
  output O2
);

  wire and_1_out, and_2_out, and_3_out, and_4_out, not_1_out;

  not not_1 (not_1_out, S);
  and and_1 (and_1_out, l1, not_1_out);
  and and_2 (and_2_out, l2, S);
  and and_3 (and_3_out, l2, not_1_out);
  and and_4 (and_4_out, l1, S);
  or or_1 (O1, and_1_out, and_2_out);
  or or_2 (O2, and_3_out, and_4_out);
endmodule

module _4bit_swap (
  input  [3:0] in_1,
  input  [3:0] in_2,
  input  in_3,
  output [3:0] out_4,
  output [3:0] out_5
);

  wire n1bit_swap_1_o1, n1bit_swap_1_o2, n1bit_swap_2_o1, n1bit_swap_2_o2, n1bit_swap_3_o1, n1bit_swap_3_o2,
       n1bit_swap_4_o1, n1bit_swap_4_o2;
  wire [1:0] bit_extender_1_out, bit_extender_2_out;
  wire [2:0] bit_extender_3_out, bit_extender_4_out;

  _1bit_swap u_1bit_swap_1 (.l1(in_1[0]), .S(in_3), .O1(n1bit_swap_1_o1), .l2(in_2[0]), .O2(n1bit_swap_1_o2));
  _1bit_swap u_1bit_swap_2 (.l1(in_1[1]), .S(in_3), .O1(n1bit_swap_2_o1), .l2(in_2[1]), .O2(n1bit_swap_2_o2));
  _1bit_swap u_1bit_swap_3 (.l1(in_1[2]), .S(in_3), .O1(n1bit_swap_3_o1), .l2(in_2[2]), .O2(n1bit_swap_3_o2));
  _1bit_swap u_1bit_swap_4 (.l1(in_1[3]), .S(in_3), .O1(n1bit_swap_4_o1), .l2(in_2[3]), .O2(n1bit_swap_4_o2));
  assign bit_extender_1_out = {{1{n1bit_swap_2_o1}}, n1bit_swap_1_o1};  // Bit_Extender bit_extender_1
  assign bit_extender_2_out = {{1{n1bit_swap_2_o2}}, n1bit_swap_1_o2};  // Bit_Extender bit_extender_2
  assign bit_extender_3_out = {{1{n1bit_swap_3_o1}}, bit_extender_1_out};  // Bit_Extender bit_extender_3
  assign bit_extender_4_out = {{1{n1bit_swap_3_o2}}, bit_extender_2_out};  // Bit_Extender bit_extender_4
  assign out_4 = {{1{n1bit_swap_4_o1}}, bit_extender_3_out};  // Bit_Extender bit_extender_5
  assign out_5 = {{1{n1bit_swap_4_o2}}, bit_extender_4_out};  // Bit_Extender bit_extender_6

  // Other names for the same wires on the sheet: ctrl = in_3
endmodule

module _4bit_sort_xier_unstable (
  input  [3:0] in_1,
  input  [3:0] in_2,
  input  [3:0] in_3,
  input  [3:0] in_4,
  output [3:0] out_5,
  output [3:0] out_6,
  output [3:0] out_7,
  output [3:0] out_8
);

  wire comparator_1_gt, comparator_2_gt, comparator_3_gt, comparator_4_gt;
  wire [3:0] n4bit_swap_1_out_4, n4bit_swap_1_out_5, n4bit_swap_2_out_4, n4bit_swap_2_out_5;

  _4bit_swap u_4bit_swap_1 (
    .in_1(in_1), .in_2(in_3), .in_3(comparator_1_gt), .out_4(n4bit_swap_1_out_4), .out_5(n4bit_swap_1_out_5));
  Comparator #(.width(4), .mode("unsigned")) comparator_1 (.a(in_1), .b(in_3), .gt(comparator_1_gt));  // open: eq, lt
  Comparator #(.width(4), .mode("unsigned")) comparator_2 (.a(in_2), .b(in_4), .gt(comparator_2_gt));  // open: eq, lt
  _4bit_swap u_4bit_swap_2 (
    .in_1(in_2), .in_2(in_4), .in_3(comparator_2_gt), .out_4(n4bit_swap_2_out_4), .out_5(n4bit_swap_2_out_5));
  Comparator #(.width(4), .mode("unsigned")) comparator_3 (
    .a(n4bit_swap_1_out_4), .b(n4bit_swap_2_out_4), .gt(comparator_3_gt));  // open: eq, lt
  Comparator #(.width(4), .mode("unsigned")) comparator_4 (
    .a(n4bit_swap_1_out_5), .b(n4bit_swap_2_out_5), .gt(comparator_4_gt));  // open: eq, lt
  _4bit_swap u_4bit_swap_3 (
    .in_1(n4bit_swap_1_out_4), .in_2(n4bit_swap_2_out_4), .in_3(comparator_3_gt), .out_4(out_5), .out_5(out_6));
  _4bit_swap u_4bit_swap_4 (
    .in_1(n4bit_swap_1_out_5), .in_2(n4bit_swap_2_out_5), .in_3(comparator_4_gt), .out_4(out_7), .out_5(out_8));
endmodule

module _4bit_sort (
  input  [3:0] in_1,
  input  [3:0] in_2,
  input  [3:0] in_3,
  input  [3:0] in_4,
  output [3:0] out_5,
  output [3:0] out_6,
  output [3:0] out_7,
  output [3:0] out_8
);

  wire comparator_1_gt, comparator_2_gt, comparator_3_gt, comparator_4_gt, comparator_5_gt;
  wire [3:0] n4bit_swap_1_out_4, n4bit_swap_1_out_5, n4bit_swap_2_out_4, n4bit_swap_2_out_5,
       n4bit_swap_3_out_5, n4bit_swap_4_out_4;

  Comparator #(.width(4), .mode("unsigned")) comparator_1 (.a(in_1), .b(in_2), .gt(comparator_1_gt));  // open: eq, lt
  Comparator #(.width(4), .mode("unsigned")) comparator_2 (.a(in_3), .b(in_4), .gt(comparator_2_gt));  // open: eq, lt
  _4bit_swap u_4bit_swap_1 (
    .in_1(in_1), .in_2(in_2), .in_3(comparator_1_gt), .out_4(n4bit_swap_1_out_4), .out_5(n4bit_swap_1_out_5));
  _4bit_swap u_4bit_swap_2 (
    .in_1(in_3), .in_2(in_4), .in_3(comparator_2_gt), .out_4(n4bit_swap_2_out_4), .out_5(n4bit_swap_2_out_5));
  Comparator #(.width(4), .mode("unsigned")) comparator_3 (
    .a(n4bit_swap_1_out_5), .b(n4bit_swap_2_out_5), .gt(comparator_3_gt));  // open: eq, lt
  Comparator #(.width(4), .mode("unsigned")) comparator_4 (
    .a(n4bit_swap_1_out_4), .b(n4bit_swap_2_out_4), .gt(comparator_4_gt));  // open: eq, lt
  _4bit_swap u_4bit_swap_3 (
    .in_1(n4bit_swap_1_out_4), .in_2(n4bit_swap_2_out_4), .in_3(comparator_4_gt), .out_4(out_5),
    .out_5(n4bit_swap_3_out_5));
  _4bit_swap u_4bit_swap_4 (
    .in_1(n4bit_swap_1_out_5), .in_2(n4bit_swap_2_out_5), .in_3(comparator_3_gt), .out_4(n4bit_swap_4_out_4),
    .out_5(out_8));
  Comparator #(.width(4)) comparator_5 (
    .a(n4bit_swap_3_out_5), .b(n4bit_swap_4_out_4), .gt(comparator_5_gt));  // open: eq, lt
  _4bit_swap u_4bit_swap_5 (
    .in_1(n4bit_swap_3_out_5), .in_2(n4bit_swap_4_out_4), .in_3(comparator_5_gt), .out_4(out_6), .out_5(out_7));
endmodule
